# Fritzing sketch DHT11 Sensor (saved by Fritzing 0.9.3b)
breadboards: 1

parts:
  Raspberry_Pi_1 = Raspberry Pi 3 [part_number=RPI-3-V1.2]
  DHT11_1 = DHT11 module
  R1 = Resistor [tolerance=±5% resistance=10k package="0402 [SMD]"]

nets:
  N1: Raspberry_Pi_1.3v3, DHT11_1.DATA, R1.Pin_0
  N2: Raspberry_Pi_1.GIPO4, DHT11_1.VCC, R1.Pin_1
  GND: Raspberry_Pi_1.GND, DHT11_1.GND

custom parts:
  DHT11 module: DHT11 black pcb module
