# Fritzing sketch Hygrometer FC-28 Sensor (saved by Fritzing 0.9.3b)
breadboards: 1

parts:
  Raspberry_Pi_1 = Raspberry Pi 3 [part_number=RPI-3-V1.2]
  Componente3 = FC-28 Soil Hygrometer Module
  Componente4 = FC-28 Soil Hygrometer Module - Probe
  Componente1 = Adafruit ADS1115 16Bit I2C ADC [part_number="Adafruit #1085"]

nets:
  N1: Raspberry_Pi_1.GPIO2, Componente1.SDA
  N2: Raspberry_Pi_1.GPIO3, Componente1.SCL
  3V3: Raspberry_Pi_1.3V3, Componente3.VCC, Componente1.VDD
  GND: Raspberry_Pi_1.GND, Componente3.GND, Componente1.ADDR, Componente1.GND
  N3: Componente3.AO, Componente1.AIN0
  N4: Componente3.POS, Componente4.POS
  N5: Componente3.NEG, Componente4.NEG

custom parts:
  FC-28 Soil Hygrometer Module: The FC-28 is a soil hygrometer module that uses the Texas Instruments LM393 comparator chip to provide an analog measurement of soil humidity. The digital output is high when soil moisture is over a certain threshold, as determined by adjusting the potentiometer.
  FC-28 Soil Hygrometer Module - Probe: The FC-28 is a soil hygrometer module that uses the Texas Instruments LM393 comparator chip to provide an analog measurement of soil humidity.
  Adafruit ADS1115 16Bit I2C ADC: For microcontrollers without an analog-to-digital converter or when you want a higher-precision ADC, the ADS1115 provides 16-bit precision at 860 samples/second over I2C. The chip can be configured as 4 single-ended input channels, or two differential channels. As a nice bonus, it even includes a programmable gain amplifier, up to x16, to help boost up smaller single/differential signals to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
