# Fritzing sketch LED brightness (saved by Fritzing 0.9.3b)
breadboards: 1

parts:
  Raspberry_Pi_1 = Raspberry Pi 3 [part_number=RPI-3-V1.2]
  LED20 = smd LED [color="Red (633nm)" package="0603 [SMD]"]
  R19 = Resistor [tolerance=±5% resistance=330 package="0402 [SMD]"]

nets:
  N1: Raspberry_Pi_1.GND, LED20.cathode
  N2: Raspberry_Pi_1.GIPO21, R19.Pin_0
  N3: LED20.anode, R19.Pin_1
