# Fritzing sketch LED on and off (saved by Fritzing 0.9.3b)
breadboards: 1

parts:
  Raspberry_Pi_1 = Raspberry Pi 3 [part_number=RPI-3-V1.2]
  R1 = Resistor [tolerance=±5% resistance=330 package="0402 [SMD]"]
  LED1 = smd LED [color="Red (633nm)" package="0603 [SMD]"]
  LED2 = smd LED [color="Red (633nm)" package="0603 [SMD]"]
  LED3 = smd LED [color="Red (633nm)" package="0603 [SMD]"]
  LED4 = smd LED [color="Red (633nm)" package="0603 [SMD]"]
  LED5 = smd LED [color="Red (633nm)" package="0603 [SMD]"]
  LED6 = smd LED [color="Red (633nm)" package="0603 [SMD]"]
  LED7 = smd LED [color="Red (633nm)" package="0603 [SMD]"]
  LED8 = smd LED [color="Red (633nm)" package="0603 [SMD]"]
  LED9 = smd LED [color="Red (633nm)" package="0603 [SMD]"]
  LED10 = smd LED [color="Red (633nm)" package="0603 [SMD]"]
  LED11 = smd LED [color="Red (633nm)" package="0603 [SMD]"]
  LED12 = smd LED [color="Red (633nm)" package="0603 [SMD]"]
  LED13 = smd LED [color="Red (633nm)" package="0603 [SMD]"]
  LED14 = smd LED [color="Red (633nm)" package="0603 [SMD]"]
  LED15 = smd LED [color="Red (633nm)" package="0603 [SMD]"]
  LED16 = smd LED [color="Red (633nm)" package="0603 [SMD]"]
  LED17 = smd LED [color="Red (633nm)" package="0603 [SMD]"]
  LED18 = smd LED [color="Red (633nm)" package="0603 [SMD]"]
  LED19 = smd LED [color="Red (633nm)" package="0603 [SMD]"]
  LED20 = smd LED [color="Red (633nm)" package="0603 [SMD]"]
  LED21 = smd LED [color="Red (633nm)" package="0603 [SMD]"]
  LED22 = smd LED [color="Red (633nm)" package="0603 [SMD]"]
  LED23 = smd LED [color="Red (633nm)" package="0603 [SMD]"]
  LED24 = smd LED [color="Red (633nm)" package="0603 [SMD]"]
  LED25 = smd LED [color="Red (633nm)" package="0603 [SMD]"]
  LED26 = smd LED [color="Red (633nm)" package="0603 [SMD]"]
  R2 = Resistor [tolerance=±5% resistance=330 package="0402 [SMD]"]
  R3 = Resistor [tolerance=±5% resistance=330 package="0402 [SMD]"]
  R4 = Resistor [tolerance=±5% resistance=330 package="0402 [SMD]"]
  R5 = Resistor [tolerance=±5% resistance=330 package="0402 [SMD]"]
  R6 = Resistor [tolerance=±5% resistance=330 package="0402 [SMD]"]
  R7 = Resistor [tolerance=±5% resistance=330 package="0402 [SMD]"]
  R8 = Resistor [tolerance=±5% resistance=330 package="0402 [SMD]"]
  R9 = Resistor [tolerance=±5% resistance=330 package="0402 [SMD]"]
  R10 = Resistor [tolerance=±5% resistance=330 package="0402 [SMD]"]
  R11 = Resistor [tolerance=±5% resistance=330 package="0402 [SMD]"]
  R12 = Resistor [tolerance=±5% resistance=330 package="0402 [SMD]"]
  R13 = Resistor [tolerance=±5% resistance=330 package="0402 [SMD]"]
  R14 = Resistor [tolerance=±5% resistance=330 package="0402 [SMD]"]
  R15 = Resistor [tolerance=±5% resistance=330 package="0402 [SMD]"]
  R16 = Resistor [tolerance=±5% resistance=330 package="0402 [SMD]"]
  R17 = Resistor [tolerance=±5% resistance=330 package="0402 [SMD]"]
  R18 = Resistor [tolerance=±5% resistance=330 package="0402 [SMD]"]
  R19 = Resistor [tolerance=±5% resistance=330 package="0402 [SMD]"]
  R20 = Resistor [tolerance=±5% resistance=330 package="0402 [SMD]"]
  R21 = Resistor [tolerance=±5% resistance=330 package="0402 [SMD]"]
  R22 = Resistor [tolerance=±5% resistance=330 package="0402 [SMD]"]
  R23 = Resistor [tolerance=±5% resistance=330 package="0402 [SMD]"]
  R24 = Resistor [tolerance=±5% resistance=330 package="0402 [SMD]"]
  R25 = Resistor [tolerance=±5% resistance=330 package="0402 [SMD]"]
  R26 = Resistor [tolerance=±5% resistance=330 package="0402 [SMD]"]

nets:
  N1: Raspberry_Pi_1.GPIO2, R1.Pin_0
  N2: Raspberry_Pi_1.GPIO3, R2.Pin_0
  N3: Raspberry_Pi_1.GIPO4, R3.Pin_0
  N4: Raspberry_Pi_1.GIPO17, R15.Pin_0
  N5: Raspberry_Pi_1.GIPO27, R25.Pin_0
  N6: Raspberry_Pi_1.GIPO22, R20.Pin_0
  N7: Raspberry_Pi_1.GIPO10, R7.Pin_0
  N8: Raspberry_Pi_1.GIPO9, R8.Pin_0
  N9: Raspberry_Pi_1.GIPO11, R9.Pin_0
  N10: Raspberry_Pi_1.GIPO5, R4.Pin_0
  N11: Raspberry_Pi_1.GIPO6, R5.Pin_0
  N12: Raspberry_Pi_1.GIPO13, R14.Pin_0
  N13: Raspberry_Pi_1.GIPO19, R18.Pin_0
  N14: Raspberry_Pi_1.GIPO26, R22.Pin_0
  N15: Raspberry_Pi_1.GND, LED1.cathode, LED2.cathode, LED3.cathode, LED4.cathode, LED5.cathode, LED6.cathode, LED7.cathode, LED8.cathode, LED9.cathode, LED10.cathode, LED11.cathode, LED12.cathode, LED13.cathode, LED14.cathode, LED15.cathode, LED16.cathode, LED17.cathode, LED18.cathode, LED19.cathode, LED20.cathode, LED21.cathode, LED22.cathode, LED23.cathode, LED24.cathode, LED25.cathode, LED26.cathode
  N16: Raspberry_Pi_1.GIPO21, R19.Pin_0
  N17: Raspberry_Pi_1.GIPO20, R24.Pin_0
  N18: Raspberry_Pi_1.GIPO16, R11.Pin_0
  N19: Raspberry_Pi_1.GIPO12, R17.Pin_0
  N20: Raspberry_Pi_1.GIPO7, R6.Pin_0
  N21: Raspberry_Pi_1.GIPO8, R10.Pin_0
  N22: Raspberry_Pi_1.GIPO25, R23.Pin_0
  N23: Raspberry_Pi_1.GIPO24, R26.Pin_0
  N24: Raspberry_Pi_1.GIPO23, R21.Pin_0
  N25: Raspberry_Pi_1.GIPO18, R12.Pin_0
  N26: Raspberry_Pi_1.GIPO15, R16.Pin_0
  N27: Raspberry_Pi_1.GIPO14, R13.Pin_0
  N28: R1.Pin_1, LED1.anode
  N29: LED2.anode, R2.Pin_1
  N30: LED3.anode, R3.Pin_1
  N31: LED4.anode, R4.Pin_1
  N32: LED5.anode, R5.Pin_1
  N33: LED6.anode, R6.Pin_1
  N34: LED7.anode, R10.Pin_1
  N35: LED8.anode, R8.Pin_1
  N36: LED9.anode, R7.Pin_1
  N37: LED10.anode, R9.Pin_1
  N38: LED11.anode, R17.Pin_1
  N39: LED12.anode, R14.Pin_1
  N40: LED13.anode, R13.Pin_1
  N41: LED14.anode, R16.Pin_1
  N42: LED15.anode, R11.Pin_1
  N43: LED16.anode, R15.Pin_1
  N44: LED17.anode, R12.Pin_1
  N45: LED18.anode, R18.Pin_1
  N46: LED19.anode, R24.Pin_1
  N47: LED20.anode, R19.Pin_1
  N48: LED21.anode, R20.Pin_1
  N49: LED22.anode, R21.Pin_1
  N50: LED23.anode, R26.Pin_1
  N51: LED24.anode, R23.Pin_1
  N52: LED25.anode, R22.Pin_1
  N53: LED26.anode, R25.Pin_1
