# Fritzing sketch Pyroelectric HC-SR501 Sensor (saved by Fritzing 0.9.3b)
breadboards: 1

parts:
  PIR1 = PIR sensor
  Raspberry_Pi_1 = Raspberry Pi 3 [part_number=RPI-3-V1.2]

nets:
  VDD: PIR1.VDD, Raspberry_Pi_1.3v3
  N1: PIR1.SIG, Raspberry_Pi_1.GPIO23
  GND: PIR1.GND, Raspberry_Pi_1.GND
